# Fritzing sketch FETCH_HEAD (saved by Fritzing 0.9.3b)
breadboards: 1

parts:
  Composant1 = Arduino Uno (Rev3) - ICSP
  R1 = Resistor [tolerance=±5% resistance=1M package=THT]
  L1 = Inductor [package="400 mil [THT]"]
  R2 = Resistor [tolerance=±5% resistance=500 package=THT]

nets:
  Electrode: Composant1.A0, R1.Pin_1, L1.pin_0
  GND: Composant1.GND, R1.Pin_0
  N1: Composant1.D8, R2.Pin_1
  N2: L1.pin_1, R2.Pin_0

// code stored in the sketch: PWM_Freq4.ino
//****************************************************************************************
// PWM Square Wave Generator
// VLO 2013-2014
//****************************************************************************************


const int outPin = 9; // output pin
const float maxFreq = 16000000; //max freq supported by Arduino (16MHz)

void setup()
{

  Serial.begin(115200); //for sending A0 pin values
  
  pinMode(outPin,OUTPUT);        //Signal generator pin
  
  setFrequency(500); //generate a square wave (in this case at 1000Hz)
  
  //for test
  //Serial.println();
  //Serial.println(ICR1);
  //Serial.println(TCCR1B);
}

void loop()
{


  int val = analogRead(0);                                              
  Serial.write( 0xff );                                                         
  Serial.write( (val >> 8) & 0xff );                                            
  Serial.write( val & 0xff );
 
}

//set frequency (Hz)
//min frequency: 0.24 Hz
//max frequency: 8MHz
void setFrequency(float frequency)
{
 
  if(frequency >=0.24 || frequency <=8000000)
  {
    
    TCCR1A=0b10000010;        // Set up frequency generator, mode 14 (Fast PWM)
    //WGM11 = 1, COM1A1 = 1
    //Fast PWM: TOP=ICR1, update of OCR1x=BOTTOM, TOV1 Flag Set on TOP
    
  
    unsigned int v=0;
    int indscale=0;
    float prescale[] = {1.0,8.0,64.0,256.0,1024.0};
    float period=1/frequency;
    
    while(v==0)
    {
      float curfreq=maxFreq/prescale[indscale];
      float tickperiod=1/curfreq;
      float nbtick=period/tickperiod;
     
      if(nbtick>65535)
      {
        indscale=indscale+1;
      }
      else
      {
        v=nbtick;
      }

    }
    
    int c=prescale[indscale];
    
     switch (c) {
      
         case 1: TCCR1B=0b00011001; break;
         case 8: TCCR1B=0b00011010; break;
         case 64: TCCR1B=0b00011011; break;
         case 256: TCCR1B=0b00011100; break;
         case 1024: TCCR1B=0b00011101; break;
         default: TCCR1B=0b00011000;
     }
    
    //WGM12 = 1, WGM13 = 1
    
    //three last bit of TCCR1B:    CS12   CS11   CS10
    // 0: no clock (timer stopped)  0      0      0
    // clk/1: no prescaling         0      0      1 
    // clk/8                        0      1      0
    // clk/64                       0      1      1
    // clk/256                      1      0      0
    // clk/1024                     1      0      1

    
    ICR1=v; //pulse duration = ICR1 value x time per counter tick
    
    //for 16Mhz (chip frequency)
    //Prescale	Time per counter tick
    //1	        0.0625 uS
    //8	        0.5 uS
    //64	4 uS
    //256	16 uS
    //1024	64uS
    
    OCR1A=v/2; //Output Compare Register //low state

  }
  
  
}
