# Fritzing sketch ORIG_HEAD (saved by Fritzing 0.9.3b)
breadboards: 1

parts:
  Composant1 = Arduino Uno (Rev3) - ICSP
  L1 = Inductor [inductance=10mH package="400 mil [THT]"]
  D1 = Rectifier Diode [part_number=1N4001 package="300 mil [THT]"]
  R2 = Resistor [tolerance=±5% resistance=1M package=THT]
  R3 = Resistor [tolerance=±5% resistance=220 package=THT]
  C1 = Ceramic Capacitor [capacitance=100nF package="100 mil [THT, multilayer]"]
  C2 = Ceramic Capacitor [capacitance=10nF package="100 mil [THT, multilayer]"]
  R1 = Resistor [tolerance=±5% resistance=50k package=THT]

nets:
  N1: Composant1.A0, D1.cathode, R2.Pin_0, C1.1
  N2: Composant1.D9_PWM, R1.Pin_0
  GND: Composant1.GND, R2.Pin_1, R3.Pin_1, C1.0
  N3: L1.pin_0, D1.anode, C2.0
  N4: L1.pin_1, R3.Pin_0, R1.Pin_1
  Electrode: C2.1

// code stored in the sketch: Arduino_sensing.ino
//****************************************************************************************
// Illutron take on Disney style capacitive touch sensor using only passives and Arduino
// Dzl 2012
//****************************************************************************************


//                              10n
// PIN 9 --[10k]-+-----10mH---+--||-- OBJECT
//               |            |
//              3.3k          |
//               |            V 1N4148 diode
//              GND           |
//                            |
//Analog 0 ---+------+--------+
//            |      |
//          100pf   1MOmhm
//            |      |
//           GND    GND



#define SET(x,y) (x |=(1<<y))				//-Bit set/clear macros
#define CLR(x,y) (x &= (~(1<<y)))       		// |
#define CHK(x,y) (x & (1<<y))           		// |
#define TOG(x,y) (x^=(1<<y))            		//-+



#define N 160  //How many frequencies

float results[N];            //-Filtered result buffer
float freq[N];            //-Filtered result buffer
int sizeOfArray = N;

 
   
   

void setup()
{
  
  
  TCCR1A=0b10000010;        //-Set up frequency generator
  TCCR1B=0b00011001;        //-+
  ICR1=110;
  OCR1A=55;

  pinMode(9,OUTPUT);        //-Signal generator pin
  pinMode(8,OUTPUT);        //-Sync (test) pin

  Serial.begin(115200);

  for(int i=0;i<N;i++)      //-Preset results
    results[i]=0;         //-+
}

void loop()
{
  unsigned int d;

  int counter = 0;
  for(unsigned int d=0;d<N;d++)
  {
    int v=analogRead(0);    //-Read response signal
    CLR(TCCR1B,0);          //-Stop generator
    TCNT1=0;                //-Reload new frequency
    ICR1=d;                 // |
    OCR1A=d/2;              //-+
    SET(TCCR1B,0);          //-Restart generator

    results[d]=results[d]*0.5+(float)(v)*0.5; //Filter results
    Serial.println(TCCR1B);
    
 //   plot(v,0);              //-Display
 //   plot(results[d],1);
  // delayMicroseconds(1);
  }
  delay(10000);


    //PlottArray(1,freq,results); 
 

  TOG(PORTB,0);            //-Toggle pin 8 after each sweep (good for scope)
}
